# Fritzing sketch interrupt_switch_wiring (saved by Fritzing 0.9.2b)
breadboards: 1

parts:
  Part1 = Arduino Uno (Rev3)
  S1 = Pushbutton [package="[THT]"]
  S2 = Pushbutton [package="[THT]"]

nets:
  N1: Part1.D2, Part1.D3_PWM, Part1.5V, S1.Pin_3, S1.Pin_4, S2.Pin_1, S2.Pin_2
  N2: S1.Pin_1, S1.Pin_2
  N3: S2.Pin_3, S2.Pin_4
